// Logisim project alu.circ as structural Verilog: 1 circuit, main circuit alu
module alu (
  input  [31:0] A,
  input  [31:0] B,
  input  [3:0] ALUSel,
  output [31:0] Result
);

  wire comparator_1_lt, comparator_2_lt, comparator_3_lt, comparator_4_lt, comparator_5_lt, comparator_6_lt,
       comparator_7_lt, xor_2_out;
  wire [4:0] bit_extender_1_out, bit_extender_2_out, bit_extender_3_out;
  wire [31:0] add, adder_2_out, and1, divu, mulh, mulhu, mult, multiplexer_2_out, multiplexer_3_out,
       multiplexer_4_out, multiplexer_5_out, multiplier_3_cout, multiplier_4_cout, negator_1_out,
       negator_2_out, negator_3_out, negator_4_out, negator_5_out, or1, remu, sll1, slt, sra1, srl1, sub,
       xor1;

  Subtractor #(.width(32)) subtractor_1 (.a(A), .b(B), .out(sub));  // open: bin, bout
  Divider #(.width(32)) divider_1 (.a(A), .b(B), .out(divu), .rem(remu));  // open: upper
  Multiplier #(.width(32)) multiplier_1 (.a(A), .b(B), .out(mult));  // open: cin, cout
  Multiplier #(.width(32)) multiplier_2 (.a(A), .b(B), .cout(mulhu));  // open: out, cin
  Bit_Extender #(.in_width(32), .out_width(5)) bit_extender_1 (.in(B), .out(bit_extender_1_out));
  Bit_Extender #(.in_width(32), .out_width(5)) bit_extender_2 (.in(B), .out(bit_extender_2_out));
  Bit_Extender #(.in_width(32), .out_width(5)) bit_extender_3 (.in(B), .out(bit_extender_3_out));
  Adder #(.width(32)) adder_1 (.a(A), .b(B), .out(add));  // open: cin, cout
  assign and1 = A & B;  // AND_Gate and_1, 32 bits wide
  assign or1 = A | B;  // OR_Gate or_1, 32 bits wide
  assign xor1 = A ^ B;  // XOR_Gate xor_1, 32 bits wide
  Shifter #(.width(32), .shift("lr")) shifter_1 (.in(A), .\dist (bit_extender_1_out), .out(srl1));
  Shifter #(.width(32), .shift("ar")) shifter_2 (.in(A), .\dist (bit_extender_2_out), .out(sra1));
  Shifter #(.width(32)) shifter_3 (.in(A), .\dist (bit_extender_3_out), .out(sll1));
  Comparator #(.width(32)) comparator_1 (.a(A), .b(B), .lt(comparator_1_lt));  // open: gt, eq
  assign slt = {{31{1'b0}}, comparator_1_lt};  // Bit_Extender bit_extender_4
  Multiplexer #(.select(4), .width(32), .enable("false")) multiplexer_1 (
    .in0(add), .in1(and1), .in2(or1), .in3(xor1), .in4(srl1), .in5(sra1), .in6(sll1), .in7(slt), .in8(divu),
    .in9(remu), .in10(mult), .in11(mulhu), .in12(sub), .in13(B), .in14(mulh), .out(Result), .sel(ALUSel));  // open: in15
  Negator #(.width(32)) negator_1 (.in(A), .out(negator_1_out));
  Negator #(.width(32)) negator_2 (.in(B), .out(negator_2_out));
  Comparator #(.width(32)) comparator_2 (.a(A), .b({32{1'b0}}), .lt(comparator_2_lt));  // open: gt, eq
  Comparator #(.width(32)) comparator_3 (.a(B), .b({32{1'b0}}), .lt(comparator_3_lt));  // open: gt, eq
  Multiplexer #(.width(32), .enable("false")) multiplexer_2 (
    .in0(A), .in1(negator_1_out), .out(multiplexer_2_out), .sel(comparator_2_lt));
  Multiplexer #(.width(32), .enable("false")) multiplexer_3 (
    .in0(B), .in1(negator_2_out), .out(multiplexer_3_out), .sel(comparator_3_lt));
  Negator #(.width(32)) negator_3 (.in(A), .out(negator_3_out));
  Negator #(.width(32)) negator_4 (.in(B), .out(negator_4_out));
  Multiplier #(.width(32)) multiplier_3 (
    .a(multiplexer_2_out), .b(multiplexer_3_out), .cout(multiplier_3_cout));  // open: out, cin
  Adder #(.width(32)) adder_2 (.a(multiplier_3_cout), .b(32'h1), .out(adder_2_out));  // open: cin, cout
  Comparator #(.width(32)) comparator_4 (.a(A), .b({32{1'b0}}), .lt(comparator_4_lt));  // open: gt, eq
  Comparator #(.width(32)) comparator_5 (.a(B), .b({32{1'b0}}), .lt(comparator_5_lt));  // open: gt, eq
  Comparator #(.width(32)) comparator_6 (.a(A), .b({32{1'b0}}), .lt(comparator_6_lt));  // open: gt, eq
  Comparator #(.width(32)) comparator_7 (.a(B), .b({32{1'b0}}), .lt(comparator_7_lt));  // open: gt, eq
  Multiplexer #(.width(32), .enable("false")) multiplexer_4 (
    .in0(A), .in1(negator_3_out), .out(multiplexer_4_out), .sel(comparator_4_lt));
  Multiplexer #(.width(32), .enable("false")) multiplexer_5 (
    .in0(B), .in1(negator_4_out), .out(multiplexer_5_out), .sel(comparator_5_lt));
  Negator #(.width(32)) negator_5 (.in(adder_2_out), .out(negator_5_out));
  xor xor_2 (xor_2_out, comparator_6_lt, comparator_7_lt);
  Multiplier #(.width(32)) multiplier_4 (
    .a(multiplexer_4_out), .b(multiplexer_5_out), .cout(multiplier_4_cout));  // open: out, cin
  Multiplexer #(.width(32), .enable("false")) multiplexer_6 (
    .in0(multiplier_4_cout), .in1(negator_5_out), .out(mulh), .sel(xor_2_out));

  // Other names for the same wires on the sheet: bsel[31:0] = B

  // Notes on the sheet:
  //   INPUTS to your circuit
  //   DON'T CHANGE THE LOCATIONS OF THE INPUTS AND OUTPUTS!
  //   OUTPUT from your circuit
endmodule
