// Logisim project regfile.circ as structural Verilog: 1 circuit, main circuit main
module main (
  input  [4:0] rs1,
  input  [4:0] rs2,
  input  [4:0] rd,
  input  [31:0] Write_Data,
  input  RegWEn,
  input  clk,
  input  in_7,
  input  in_8,
  input  in_9,
  input  in_10,
  input  in_11,
  input  in_12,
  input  in_13,
  input  in_14,
  input  in_15,
  input  in_16,
  output [31:0] ra,
  output [31:0] sp,
  output [31:0] t0,
  output [31:0] t1,
  output [31:0] t2,
  output [31:0] s0,
  output [31:0] s1,
  output [31:0] a0,
  output [31:0] Read_Data_1,
  output [31:0] Read_Data_2
);

  wire x0_we, x1_we, x2_we, x5_we, x6_we, x7_we, x8_we, x9_we, x10_we;
  wire [31:0] x0_in, x0_out, x1_in, x2_in, x5_in, x6_in, x7_in, x8_in, x9_in, x10_in;

  Demultiplexer #(.select(5), .width(32), .enable("false")) demultiplexer_1 (
    .out1(x1_in), .out2(x2_in), .out5(x5_in), .out6(x6_in), .out7(x7_in), .out8(x8_in), .out9(x9_in),
    .out10(x10_in), .in(Write_Data), .sel(rd));  // open: out0, out3, out4, out11, out12, out13, out14, out15, out16, out17, out18, out19, out20, out21, out22, out23, out24, out25, out26, out27, out28, out29, out30, out31
  Demultiplexer #(.select(5), .enable("false")) demultiplexer_2 (
    .out0(x0_we), .out1(x1_we), .out2(x2_we), .out5(x5_we), .out6(x6_we), .out7(x7_we), .out8(x8_we),
    .out9(x9_we), .out10(x10_we), .in(RegWEn), .sel(rd));  // open: out3, out4, out11, out12, out13, out14, out15, out16, out17, out18, out19, out20, out21, out22, out23, out24, out25, out26, out27, out28, out29, out30, out31
  Register #(.width(32)) x1 (.D(x1_in), .en(x1_we), .clk(clk), .Q(ra), .clr(in_9));
  Register #(.width(32)) x2 (.D(x2_in), .en(x2_we), .clk(clk), .Q(sp), .clr(in_12));
  Register #(.width(32)) x5 (.D(x5_in), .en(x5_we), .clk(clk), .Q(t0), .clr(in_14));
  Register #(.width(32)) x6 (.D(x6_in), .en(x6_we), .clk(clk), .Q(t1), .clr(in_16));
  Register #(.width(32)) x0 (.D(x0_in), .en(in_7), .clk(clk), .Q(x0_out), .clr(in_8));
  Multiplexer #(.select(5), .width(32), .enable("false")) multiplexer_1 (
    .in0(x0_out), .in1(ra), .in2(sp), .in5(t0), .in6(t1), .in7(t2), .in8(s0), .in9(s1), .in10(a0),
    .out(Read_Data_1), .sel(rs1));  // open: in3, in4, in11, in12, in13, in14, in15, in16, in17, in18, in19, in20, in21, in22, in23, in24, in25, in26, in27, in28, in29, in30, in31
  Multiplexer #(.select(5), .width(32), .enable("false")) multiplexer_2 (
    .in0(x0_out), .in1(ra), .in2(sp), .in5(t0), .in6(t1), .in7(t2), .in8(s0), .in9(s1), .in10(a0),
    .out(Read_Data_2), .sel(rs2));  // open: in3, in4, in11, in12, in13, in14, in15, in16, in17, in18, in19, in20, in21, in22, in23, in24, in25, in26, in27, in28, in29, in30, in31
  Register #(.width(32)) x7 (.D(x7_in), .en(x7_we), .clk(clk), .Q(t2), .clr(in_10));
  Register #(.width(32)) x8 (.D(x8_in), .en(x8_we), .clk(clk), .Q(s0), .clr(in_11));
  Register #(.width(32)) x9 (.D(x9_in), .en(x9_we), .clk(clk), .Q(s1), .clr(in_13));
  Register #(.width(32)) x10 (.D(x10_in), .en(x10_we), .clk(clk), .Q(a0), .clr(in_15));

  // Other names for the same wires on the sheet: read_data1[31:0] = Read_Data_1; read_data2[31:0] = Read_Data_2;
  //   read_reg1[4:0] = rs1; read_reg2[4:0] = rs2; write_en = RegWEn; write_reg[4:0] = rd; x1_out[31:0] = ra;
  //   x2_out[31:0] = sp; x5_out[31:0] = t0; x6_out[31:0] = t1; x7_out[31:0] = t2; x8_out[31:0] = s0;
  //   x9_out[31:0] = s1; x10_out[31:0] = a0

  // Notes on the sheet:
  //   INPUTS to your circuit
  //   DON'T CHANGE THE LOCATIONS OF THE INPUTS AND OUTPUTS!
  //   These are DEBUG/TEST outputs from your circuit.
  //   OUTPUTS from your circuit
endmodule
